# Fritzing sketch automated-rc-car (saved by Fritzing 0.9.3b)
circuit board: 8.46667cm x 5.64444cm
breadboards: 1

parts:
  Part1 = Arduino Uno (Rev3) - ICSP
  hc-sr1 = hc-sr04
  hc-sr2 = hc-sr04
  hc-sr3 = hc-sr04
  M1 = Dagu DGServo 9g (Pan and tilt) [part_number=RS001B]

nets:
  N1: Part1.ICSP_SCK, Part1.ICSP_MOSI, Part1.D10_PWM/SS, Part1.D11_PWM/MOSI, Part1.D12/MISO, Part1.D13/SCK, hc-sr1.Trig, hc-sr2.Trig, hc-sr3.Trig
  VCC: Part1.5V, hc-sr1.VCC, hc-sr2.VCC, hc-sr3.VCC, M1.vcc
  N2: Part1.D8, Part1.D9_PWM, Part1.D6_PWM, hc-sr1.Echo, hc-sr2.Echo, hc-sr3.Echo, M1.pulse
  GND: Part1.GND, hc-sr1.GND, hc-sr2.GND, hc-sr3.GND, M1.gnd

// code stored in the sketch: bike-sensors.ino
const triggerPinFL
const echoPinFL

const triggerPinFR
const echoPinFR

const triggerPinB
const echoPinB
