# Fritzing sketch pi-zero-rc-car (saved by Fritzing 0.9.3b)
breadboards: 1

parts:
  Raspberry_Pi_Zero1 = Raspberry Pi Zero
  hc-sr1 = hc-sr04
  hc-sr2 = hc-sr04
  hc-sr3 = hc-sr04
  R1 = Resistor [tolerance=±5% resistance=1k package=THT]

nets:
  GND: Raspberry_Pi_Zero1.GND, hc-sr1.GND, hc-sr2.GND, hc-sr3.GND
  VCC: Raspberry_Pi_Zero1.5V, hc-sr1.VCC, hc-sr2.VCC, hc-sr3.VCC
  N1: hc-sr3.Echo, R1.Pin_0
